// Logisim project single_cycle_mips_8bit.circ as structural Verilog: 4 circuits, main circuit main
module main (
  input  [1:0] zero_reg,
  input  Reset,
  output [1:0] rd,
  output [1:0] rs,
  output [1:0] rt
);

  wire Clock_out, control_1_alucontrol, control_1_alusrc, control_1_memread, control_1_memtoreg,
       control_1_memwrite, control_1_regdst, control_1_regwrite;
  wire [1:0] multiplexer_1_out, multiplexer_2_out;
  wire [3:0] bit_extender_1_out;
  wire [7:0] adder_1_out, alu_1_result, multiplexer_3_out, multiplexer_4_out, Program_Counter_q, ram_1_data,
       register_file_1_readdata1, register_file_1_readdata2;
  wire [7:6] rom_1_data;

  Clock Clock (.out(Clock_out));
  Register Program_Counter (.D(adder_1_out), .Q(Program_Counter_q), .clk(Clock_out), .clr(Reset));  // open: en
  Adder adder_1 (.a(8'h1), .b(Program_Counter_q), .out(adder_1_out));  // open: cin, cout
  ROM rom_1 (.addr(Program_Counter_q), .data({rom_1_data, rt, rd, rs}));  // open: sel
  Multiplexer #(.width(2), .enable("false")) multiplexer_1 (
    .in0(rt), .in1(rs), .out(multiplexer_1_out), .sel(control_1_regdst));
  Multiplexer #(.width(2), .enable("false")) multiplexer_2 (
    .in0(zero_reg), .in1(rd), .out(multiplexer_2_out), .sel(control_1_regdst));
  Control control_1 (
    .Opcode__1(rom_1_data[7]), .Opcode__0(rom_1_data[6]), .RegDst(control_1_regdst),
    .ALUsrc(control_1_alusrc), .MemtoReg(control_1_memtoreg), .RegWrite(control_1_regwrite),
    .MemRead(control_1_memread), .MemWrite(control_1_memwrite), .ALUcontrol(control_1_alucontrol));  // open: Branch
  Register_File register_file_1 (
    .WriteData(multiplexer_4_out), .WriteReg(multiplexer_1_out), .RegWrite(control_1_regwrite),
    .Clock(Clock_out), .ReadData1(register_file_1_readdata1), .ReadReg1(multiplexer_2_out),
    .ReadData2(register_file_1_readdata2), .ReadReg2(rt));
  Multiplexer #(.width(8), .enable("false")) multiplexer_3 (
    .in0(register_file_1_readdata2), .in1({rom_1_data, rt, rd, rs}), .out(multiplexer_3_out),
    .sel(control_1_alusrc));
  Multiplexer #(.width(8), .enable("false")) multiplexer_4 (
    .in0(alu_1_result), .in1(ram_1_data), .out(multiplexer_4_out), .sel(control_1_memtoreg));
  Bit_Extender #(.out_width(4), .\type ("input")) bit_extender_1 (
    .in(alu_1_result), .out(bit_extender_1_out));  // open: extend
  ALU alu_1 (
    .Input_A(register_file_1_readdata1), .Input_B(multiplexer_3_out), .ALU_Control(control_1_alucontrol),
    .Result(alu_1_result));
  RAM #(.addrWidth(4), .bus("separate")) ram_1 (
    .addr(bit_extender_1_out), .din(register_file_1_readdata2), .data(ram_1_data), .str(control_1_memwrite),
    .clk(Clock_out), .ld(control_1_memread));  // open: sel, clr

  // Notes on the sheet:
  //   contents of rom_1 (hex, n*v repeats v):
  //   df 90 56 a1 67 b2 77 b3 1f b4 1f b5 1f b6
endmodule

module Register_File (
  input  [7:0] WriteData,
  input  [1:0] WriteReg,
  input  [1:0] ReadReg1,
  input  [1:0] ReadReg2,
  input  RegWrite,
  input  Clock,
  output [7:0] ReadData1,
  output [7:0] ReadData2
);

  wire and_1_out, and_2_out, and_3_out, and_4_out, decoder_1_out0, decoder_1_out1, decoder_1_out2,
       decoder_1_out3;
  wire [7:0] multiplexer_1_out, multiplexer_2_out, multiplexer_3_out, multiplexer_4_out, register_1_q,
       register_2_q, register_3_q, register_4_q;

  Decoder #(.select(2), .enable("false")) decoder_1 (
    .out0(decoder_1_out0), .out1(decoder_1_out1), .out2(decoder_1_out2), .out3(decoder_1_out3), .sel(WriteReg));
  and and_1 (and_1_out, decoder_1_out0, RegWrite);
  and and_2 (and_2_out, decoder_1_out1, RegWrite);
  and and_3 (and_3_out, decoder_1_out2, RegWrite);
  and and_4 (and_4_out, decoder_1_out3, RegWrite);
  Multiplexer #(.width(8), .enable("false")) multiplexer_1 (
    .in0(register_1_q), .in1(WriteData), .out(multiplexer_1_out), .sel(and_1_out));
  Multiplexer #(.width(8), .enable("false")) multiplexer_2 (
    .in0(register_2_q), .in1(WriteData), .out(multiplexer_2_out), .sel(and_2_out));
  Multiplexer #(.width(8), .enable("false")) multiplexer_3 (
    .in0(register_3_q), .in1(WriteData), .out(multiplexer_3_out), .sel(and_3_out));
  Multiplexer #(.width(8), .enable("false")) multiplexer_4 (
    .in0(register_4_q), .in1(WriteData), .out(multiplexer_4_out), .sel(and_4_out));
  Register register_1 (.D(multiplexer_1_out), .Q(register_1_q), .clk(Clock));  // open: en, clr
  Register register_2 (.D(multiplexer_2_out), .Q(register_2_q), .clk(Clock));  // open: en, clr
  Register register_3 (.D(multiplexer_3_out), .Q(register_3_q), .clk(Clock));  // open: en, clr
  Register register_4 (.D(multiplexer_4_out), .Q(register_4_q), .clk(Clock));  // open: en, clr
  Multiplexer #(.select(2), .width(8), .enable("false")) multiplexer_5 (
    .in0(register_1_q), .in1(register_2_q), .in2(register_3_q), .in3(register_4_q), .out(ReadData1),
    .sel(ReadReg1));
  Multiplexer #(.select(2), .width(8), .enable("false")) multiplexer_6 (
    .in0(register_1_q), .in1(register_2_q), .in2(register_3_q), .in3(register_4_q), .out(ReadData2),
    .sel(ReadReg2));

  // Notes on the sheet:
  //   Register File 8x8-bits
endmodule

module ALU (
  input  [7:0] Input_A,
  input  [7:0] Input_B,
  input  ALU_Control,
  output [7:0] Result
);

  wire [7:0] adder_1_out, subtractor_1_out;

  Subtractor subtractor_1 (.a(Input_A), .b(Input_B), .out(subtractor_1_out));  // open: bin, bout
  Adder adder_1 (.a(Input_A), .b(Input_B), .out(adder_1_out));  // open: cin, cout
  Multiplexer #(.width(8), .enable("false")) multiplexer_1 (
    .in0(subtractor_1_out), .in1(adder_1_out), .out(Result), .sel(ALU_Control));
endmodule

module Control (
  input  Opcode__1,
  input  Opcode__0,
  output RegDst,
  output ALUsrc,
  output MemtoReg,
  output RegWrite,
  output MemRead,
  output MemWrite,
  output Branch,
  output ALUcontrol
);

  wire not_2_out, not_3_out;

  not not_1 (RegDst, Opcode__1);
  or or_1 (RegWrite, RegDst, Opcode__0);
  not not_2 (not_2_out, RegDst);
  not not_3 (not_3_out, Opcode__0);
  not not_4 (Branch, 1'b1);
  and and_1 (MemtoReg, Opcode__1, Opcode__0);
  and and_2 (MemRead, not_2_out, Opcode__0);
  and and_3 (MemWrite, not_2_out, not_3_out);
  or or_2 (ALUcontrol, Opcode__1, Opcode__0);

  assign ALUsrc = Opcode__1;
endmodule
